// Logisim project CalculatorCircuit.circ as structural Verilog: 11 circuits, main circuit Computer
module main (
);

  wire _0_out, _1_out, _2_out, _3_out, _4_out, _5_out, _6_out, _7_out, _8_out, _9_out, buffer_1_out,
       button_2_out, button_out, function_holder_1_out_7, priority_encoder_1_gs, R_out;
  wire [1:0] function_holder_1_out_6;
  wire [3:0] Main_out_6, Main_out_6_2, Main_out_7, Main_out_7_2, Main_out_7_3, Main_out_7_4, Main_out_8,
       Main_out_8_2, Main_out_8_3, Main_out_8_4, priority_encoder_1_out;
  wire [4:0] part_1_out_3, part_1_out_4, part_1_out_5, part_1_out_6, part_1_out_7, part_2_out_2,
       part_2_out_3, part_2_out_4, part_2_out_5, part_2_out_6;
  wire [15:8] Main_out_6_3;

  Hex_Digit_Display hex_digit_display_1 (.value(Main_out_6_3[15:12]));  // open: dp
  Hex_Digit_Display hex_digit_display_2 (.value(Main_out_6_3[11:8]));  // open: dp
  Hex_Digit_Display hex_digit_display_3 (.value(Main_out_6_2));  // open: dp
  Button _2 (.out(_2_out));
  Button _1 (.out(_1_out));
  Button _4 (.out(_4_out));
  Button _5 (.out(_5_out));
  Button _8 (.out(_8_out));
  Button _7 (.out(_7_out));
  Button _0 (.out(_0_out));
  Button button (.out(button_out));
  Button R (.out(R_out));
  circuit part_1 (
    .in_1(function_holder_1_out_6), .in_2(function_holder_1_out_7), .out_3(part_1_out_3),
    .out_4(part_1_out_4), .out_5(part_1_out_5), .out_6(part_1_out_6), .out_7(part_1_out_7));
  Hex_Digit_Display hex_digit_display_4 (.value(Main_out_6));  // open: dp
  DotMatrix #(.matrixrows(5)) dotmatrix_1 (
    .col0(part_1_out_3), .col1(part_1_out_4), .col2(part_1_out_5), .col3(part_1_out_6), .col4(part_1_out_7));
  Button _3 (.out(_3_out));
  Button _6 (.out(_6_out));
  Button _9 (.out(_9_out));
  Button button_2 (.out(button_2_out));
  Hex_Digit_Display hex_digit_display_5 (.value(Main_out_7_3));  // open: dp
  Hex_Digit_Display hex_digit_display_6 (.value(Main_out_7_4));  // open: dp
  Priority_Encoder #(.select(4)) priority_encoder_1 (
    .in0(_0_out), .in1(_1_out), .in2(_2_out), .in3(_3_out), .in4(_4_out), .in5(_5_out), .in6(_6_out),
    .in7(_7_out), .in8(_8_out), .in9(_9_out), .out(priority_encoder_1_out), .gs(priority_encoder_1_gs));  // open: in10, in11, in12, in13, in14, in15, en_out, en_in
  Pull_Resistor pull_resistor_1 (.node(priority_encoder_1_out));
  buf buffer_1 (buffer_1_out, priority_encoder_1_gs);
  function_holder function_holder_1 (
    .in_1(button_out), .in_2(button_2_out), .in_5(R_out), .out_6(function_holder_1_out_6),
    .out_7(function_holder_1_out_7));  // open: in_3, in_4
  Hex_Digit_Display hex_digit_display_7 (.value(Main_out_7_2));  // open: dp
  Hex_Digit_Display hex_digit_display_8 (.value(Main_out_7));  // open: dp
  Computer Main (
    .in_1(priority_encoder_1_out), .in_2(buffer_1_out), .in_3(function_holder_1_out_6),
    .in_4(function_holder_1_out_7), .in_5(R_out), .out_6({Main_out_6_3, Main_out_6_2, Main_out_6}),
    .out_7({Main_out_7_4, Main_out_7_3, Main_out_7_2, Main_out_7}),
    .out_8({Main_out_8_4, Main_out_8_3, Main_out_8_2, Main_out_8}));  // open: out_9
  DotMatrix #(.matrixrows(5)) dotmatrix_2 (
    .col0(part_2_out_2), .col1(part_2_out_3), .col2(part_2_out_4), .col3(part_2_out_5), .col4(part_2_out_6));
  circuit_2 part_2 (
    .in_1(function_holder_1_out_7), .out_2(part_2_out_2), .out_3(part_2_out_3), .out_4(part_2_out_4),
    .out_5(part_2_out_5), .out_6(part_2_out_6));
  Hex_Digit_Display hex_digit_display_9 (.value(Main_out_8_3));  // open: dp
  Hex_Digit_Display hex_digit_display_10 (.value(Main_out_8_4));  // open: dp
  Hex_Digit_Display hex_digit_display_11 (.value(Main_out_8_2));  // open: dp
  Hex_Digit_Display hex_digit_display_12 (.value(Main_out_8));  // open: dp

  // Notes on the sheet:
  //   Reset
endmodule

module function_holder (
  input  in_1,
  input  in_2,
  input  in_3,
  input  in_4,
  input  in_5,
  output [1:0] out_6,
  output out_7
);

  wire priority_encoder_1_gs;
  wire [1:0] priority_encoder_1_out;

  // Probe on priority_encoder_1_out
  Priority_Encoder #(.select(2), .disabled(0)) priority_encoder_1 (
    .in0(in_1), .in1(in_2), .in2(in_3), .in3(in_4), .out(priority_encoder_1_out), .gs(priority_encoder_1_gs));  // open: en_out, en_in
  Register #(.width(2)) register_1 (
    .D(priority_encoder_1_out), .Q(out_6), .clk(priority_encoder_1_gs), .clr(in_5));  // open: en
  Counter #(.width(1), .max('h1), .ongoal("stay")) counter_1 (
    .Q(out_7), .clk(priority_encoder_1_gs), .clr(in_5));  // open: load, D, count, carry
endmodule

module Computer (
  input  [3:0] in_1,
  input  in_2,
  input  [1:0] in_3,
  input  in_4,
  input  in_5,
  output [15:0] out_6,
  output [15:0] out_7,
  output [15:0] out_8,
  output out_9
);

  wire and_1_out, and_2_out, and_3_out, and_4_out, base_10_minus_module_1_out_12,
       base_10_minus_module_1_out_13, base_10_minus_module_2_out_8, base_10_minus_module_2_out_9,
       base_10_minus_module_2_out_10, base_10_minus_module_2_out_12, base_10_minus_module_2_out_13,
       base_10_minus_module_3_out_8, base_10_minus_module_3_out_9, base_10_minus_module_3_out_10,
       base_10_minus_module_3_out_12, base_10_minus_module_3_out_13, base_10_minus_module_4_out_8,
       base_10_minus_module_4_out_9, base_10_minus_module_4_out_10, base_10_minus_module_4_out_12,
       base_10_plus_module_1_out_5, base_10_plus_module_2_out_5, base_10_plus_module_3_out_5,
       base_10_plus_module_4_out_5, counter_2_q, counter_4_q, decoder_1_out0, decoder_1_out1, decoder_2_out0,
       decoder_2_out1, decoder_2_out2, decoder_2_out3, decoder_3_out0, decoder_3_out1, decoder_3_out2,
       decoder_3_out3, not_1_out, not_2_out;
  wire [1:0] counter_1_q, counter_3_q, register_1_q, register_6_q, subtractor_1_out, subtractor_2_out;
  wire [3:0] base_10_minus_module_1_out_11, base_10_minus_module_2_out_11, base_10_minus_module_3_out_11,
       base_10_minus_module_4_out_11, base_10_plus_module_1_out_4, base_10_plus_module_2_out_4,
       base_10_plus_module_3_out_4, base_10_plus_module_4_out_4, bit_extender_1_out, bit_extender_2_out,
       multiplier_1_out, multiplier_2_out, register_2_q, register_3_q, register_4_q, register_5_q,
       register_7_q, register_8_q, register_9_q, register_10_q;
  wire [31:0] demultiplexer_1_out0, demultiplexer_1_out1, demultiplexer_1_out2;

  Decoder #(.disabled(0), .enable("false")) decoder_1 (.out0(decoder_1_out0), .out1(decoder_1_out1), .sel(in_4));
  Decoder #(.select(2), .disabled(0), .enable("false")) decoder_2 (
    .out0(decoder_2_out0), .out1(decoder_2_out1), .out2(decoder_2_out2), .out3(decoder_2_out3),
    .sel(counter_1_q));
  Counter #(.width(2), .max('h3), .ongoal("stay"), .trigger("falling")) counter_1 (
    .count(decoder_1_out0), .Q(counter_1_q), .clk(and_1_out), .clr(in_5));  // open: load, D, carry
  and and_1 (and_1_out, decoder_1_out0, in_2);
  Register #(.width(2)) register_1 (
    .D(counter_1_q), .en(decoder_1_out0), .Q(register_1_q), .clk(and_1_out), .clr(in_5));
  Register #(.width(4)) register_2 (.D(in_1), .en(decoder_2_out0), .Q(register_2_q), .clk(and_1_out), .clr(in_5));
  Counter #(.width(1), .max('h1), .ongoal("stay")) counter_2 (
    .count(decoder_2_out3), .Q(counter_2_q), .clk(in_2), .clr(in_5));  // open: load, D, carry
  Register #(.width(4)) register_3 (.D(in_1), .en(decoder_2_out2), .Q(register_3_q), .clk(and_1_out), .clr(in_5));
  Register #(.width(4)) register_4 (.D(in_1), .en(decoder_2_out1), .Q(register_4_q), .clk(and_1_out), .clr(in_5));
  and and_2 (and_2_out, decoder_2_out3, not_1_out);
  not not_1 (not_1_out, counter_2_q);
  Register #(.width(4)) register_5 (.D(in_1), .en(and_2_out), .Q(register_5_q), .clk(and_1_out), .clr(in_5));
  Decoder #(.select(2), .disabled(0), .enable("false")) decoder_3 (
    .out0(decoder_3_out0), .out1(decoder_3_out1), .out2(decoder_3_out2), .out3(decoder_3_out3),
    .sel(counter_3_q));
  Counter #(.width(2), .max('h3), .ongoal("stay"), .trigger("falling")) counter_3 (
    .count(decoder_1_out1), .Q(counter_3_q), .clk(and_3_out), .clr(in_5));  // open: load, D, carry
  and and_3 (and_3_out, decoder_1_out1, in_2);
  Register #(.width(2)) register_6 (
    .D(counter_3_q), .en(decoder_1_out1), .Q(register_6_q), .clk(and_3_out), .clr(in_5));
  Register #(.width(4)) register_7 (.D(in_1), .en(decoder_3_out0), .Q(register_7_q), .clk(and_3_out), .clr(in_5));
  Register #(.width(4)) register_8 (.D(in_1), .en(decoder_3_out2), .Q(register_8_q), .clk(and_3_out), .clr(in_5));
  Register #(.width(4)) register_9 (.D(in_1), .en(decoder_3_out1), .Q(register_9_q), .clk(and_3_out), .clr(in_5));
  and and_4 (and_4_out, decoder_3_out3, not_2_out);
  not not_2 (not_2_out, counter_4_q);
  Counter #(.width(1), .max('h1), .ongoal("stay")) counter_4 (
    .count(decoder_3_out3), .Q(counter_4_q), .clk(in_2), .clr(in_5));  // open: load, D, carry
  Register #(.width(4)) register_10 (.D(in_1), .en(and_4_out), .Q(register_10_q), .clk(and_3_out), .clr(in_5));
  Demultiplexer #(.select(2), .width(32), .disabled(0)) demultiplexer_1 (
    .out0(demultiplexer_1_out0), .out1(demultiplexer_1_out1), .out2(demultiplexer_1_out2),
    .in({out_7, out_6}), .sel(in_3), .en(in_4));  // open: out3
  // Probe on {out_7, out_6}
  assign bit_extender_1_out = {{2{1'b0}}, subtractor_1_out};  // Bit_Extender bit_extender_1
  Subtractor #(.width(2)) subtractor_1 (.a(2'b11), .b(register_1_q), .out(subtractor_1_out));  // open: bin, bout
  Subtractor #(.width(2)) subtractor_2 (.a(2'b11), .b(register_6_q), .out(subtractor_2_out));  // open: bin, bout
  assign bit_extender_2_out = {{2{1'b0}}, subtractor_2_out};  // Bit_Extender bit_extender_2
  Base_10_plus_module base_10_plus_module_1 (
    .in_2(demultiplexer_1_out0[3:0]), .in_3(demultiplexer_1_out0[19:16]),
    .out_5(base_10_plus_module_1_out_5), .out_4(base_10_plus_module_1_out_4));  // open: in_1
  Base_10_plus_module base_10_plus_module_2 (
    .in_2(demultiplexer_1_out0[7:4]), .in_3(demultiplexer_1_out0[23:20]), .in_1(base_10_plus_module_1_out_5),
    .out_5(base_10_plus_module_2_out_5), .out_4(base_10_plus_module_2_out_4));
  Base_10_plus_module base_10_plus_module_3 (
    .in_2(demultiplexer_1_out0[11:8]), .in_3(demultiplexer_1_out0[27:24]),
    .in_1(base_10_plus_module_2_out_5), .out_5(base_10_plus_module_3_out_5),
    .out_4(base_10_plus_module_3_out_4));
  Base_10_plus_module base_10_plus_module_4 (
    .in_2(demultiplexer_1_out0[15:12]), .in_3(demultiplexer_1_out0[31:28]),
    .in_1(base_10_plus_module_3_out_5), .out_5(base_10_plus_module_4_out_5),
    .out_4(base_10_plus_module_4_out_4));
  Base_10_minus_module base_10_minus_module_1 (
    .in_3(demultiplexer_1_out1[3:0]), .in_4(demultiplexer_1_out1[19:16]),
    .out_12(base_10_minus_module_1_out_12), .in_5(base_10_minus_module_2_out_8),
    .in_6(base_10_minus_module_2_out_9), .out_13(base_10_minus_module_1_out_13),
    .in_7(base_10_minus_module_2_out_10), .out_11(base_10_minus_module_1_out_11));  // open: in_2, out_8, out_9, in_1, out_10
  Base_10_minus_module base_10_minus_module_2 (
    .in_3(demultiplexer_1_out1[7:4]), .in_4(demultiplexer_1_out1[23:20]),
    .in_2(base_10_minus_module_1_out_12), .out_8(base_10_minus_module_2_out_8),
    .out_9(base_10_minus_module_2_out_9), .in_1(base_10_minus_module_1_out_13),
    .out_10(base_10_minus_module_2_out_10), .out_12(base_10_minus_module_2_out_12),
    .in_5(base_10_minus_module_3_out_8), .in_6(base_10_minus_module_3_out_9),
    .out_13(base_10_minus_module_2_out_13), .in_7(base_10_minus_module_3_out_10),
    .out_11(base_10_minus_module_2_out_11));
  Base_10_minus_module base_10_minus_module_3 (
    .in_3(demultiplexer_1_out1[11:8]), .in_4(demultiplexer_1_out1[27:24]),
    .in_2(base_10_minus_module_2_out_12), .out_8(base_10_minus_module_3_out_8),
    .out_9(base_10_minus_module_3_out_9), .in_1(base_10_minus_module_2_out_13),
    .out_10(base_10_minus_module_3_out_10), .out_12(base_10_minus_module_3_out_12),
    .in_5(base_10_minus_module_4_out_8), .in_6(base_10_minus_module_4_out_9),
    .out_13(base_10_minus_module_3_out_13), .in_7(base_10_minus_module_4_out_10),
    .out_11(base_10_minus_module_3_out_11));
  Base_10_minus_module base_10_minus_module_4 (
    .in_3(demultiplexer_1_out1[15:12]), .in_4(demultiplexer_1_out1[31:28]),
    .in_2(base_10_minus_module_3_out_12), .out_8(base_10_minus_module_4_out_8),
    .out_9(base_10_minus_module_4_out_9), .in_1(base_10_minus_module_3_out_13),
    .out_10(base_10_minus_module_4_out_10), .out_12(base_10_minus_module_4_out_12),
    .out_11(base_10_minus_module_4_out_11));  // open: in_5, in_6, out_13, in_7
  Shifter #(.width(16), .shift("lr")) shifter_1 (
    .in({register_2_q, register_4_q, register_3_q, register_5_q}), .\dist (multiplier_1_out), .out(out_6));
  Multiplier #(.width(4)) multiplier_1 (
    .a(4'b0100), .b(bit_extender_1_out), .out(multiplier_1_out));  // open: cin, cout
  Shifter #(.width(16), .shift("lr")) shifter_2 (
    .in({register_7_q, register_9_q, register_8_q, register_10_q}), .\dist (multiplier_2_out), .out(out_7));
  Multiplier #(.width(4)) multiplier_2 (
    .a(4'b0100), .b(bit_extender_2_out), .out(multiplier_2_out));  // open: cin, cout
  assign out_8[3:0] = base_10_minus_module_1_out_11 | base_10_plus_module_1_out_4;  // OR_Gate or_1, 4 bits wide
  assign out_8[7:4] = base_10_minus_module_2_out_11 | base_10_plus_module_2_out_4;  // OR_Gate or_2, 4 bits wide
  assign out_8[11:8] = base_10_minus_module_3_out_11 | base_10_plus_module_3_out_4;  // OR_Gate or_3, 4 bits wide
  assign out_8[15:12] = base_10_minus_module_4_out_11 | base_10_plus_module_4_out_4;  // OR_Gate or_4, 4 bits wide
  or or_5 (out_9, base_10_minus_module_4_out_12, base_10_plus_module_4_out_5);
endmodule

module circuit (
  input  [1:0] in_1,
  input  in_2,
  output [4:0] out_3,
  output [4:0] out_4,
  output [4:0] out_5,
  output [4:0] out_6,
  output [4:0] out_7
);

  Multiplexer #(.select(2), .width(25), .disabled(0)) multiplexer_1 (
    .in0(25'h427c84), .in1(25'h421084), .in2(25'h1151151), .in3(25'h425484),
    .out({out_7, out_6, out_5, out_4, out_3}), .sel(in_1), .en(in_2));
endmodule

module _1_bit (
  input  First_number,
  input  Second_number,
  input  Carry,
  output Result,
  output Carry_2
);

  wire and_1_out, and_2_out, and_3_out, nand_1_out, xor_1_out;

  LED led_1 (.in(First_number));
  LED led_2 (.in(Second_number));
  Pull_Resistor pull_resistor_1 (.node(Second_number));
  Pull_Resistor pull_resistor_2 (.node(Carry));
  xor xor_1 (xor_1_out, First_number, Second_number);
  LED led_3 (.in(Carry));
  and and_1 (and_1_out, xor_1_out, Second_number);
  LED Answer (.in(xor_1_out));
  LED Answer_is_negative__0_1 (.in(and_1_out));
  xor xor_2 (Result, xor_1_out, Carry);
  nand nand_1 (nand_1_out, xor_1_out, ~and_1_out);  // NAND_Gate
  and and_2 (and_2_out, nand_1_out, Carry);
  and and_3 (and_3_out, xor_1_out, and_1_out, ~Carry);  // AND_Gate
  LED led_4 (.in(Result));
  LED led_5 (.in(Carry_2));
  or or_1 (Carry_2, and_2_out, and_3_out);

  // Notes on the sheet:
  //   1st # ~= 2nd #
endmodule

module _4_bit (
  input  [3:0] in_1,
  input  in_2,
  input  [3:0] in_3,
  output [3:0] out_4,
  output out_5
);

  wire n1_bit_1_carry_2, n1_bit_2_carry_2, n1_bit_3_carry_2;

  Pull_Resistor pull_resistor_1 (.node(in_2));
  _1_bit u_1_bit_1 (
    .First_number(in_1[0]), .Second_number(in_3[0]), .Carry(in_2), .Carry_2(n1_bit_1_carry_2),
    .Result(out_4[0]));
  _1_bit u_1_bit_2 (
    .First_number(in_1[1]), .Second_number(in_3[1]), .Carry(n1_bit_1_carry_2), .Carry_2(n1_bit_2_carry_2),
    .Result(out_4[1]));
  _1_bit u_1_bit_3 (
    .First_number(in_1[2]), .Second_number(in_3[2]), .Carry(n1_bit_2_carry_2), .Carry_2(n1_bit_3_carry_2),
    .Result(out_4[2]));
  _1_bit u_1_bit_4 (
    .First_number(in_1[3]), .Second_number(in_3[3]), .Carry(n1_bit_3_carry_2), .Carry_2(out_5),
    .Result(out_4[3]));
endmodule

module Base_10_minus_module (
  input  in_1,
  input  in_2,
  input  [3:0] in_3,
  input  [3:0] in_4,
  input  in_5,
  input  in_6,
  input  in_7,
  output out_8,
  output out_9,
  output out_10,
  output [3:0] out_11,
  output out_12,
  output out_13
);

  wire and_1_out, and_2_out, and_3_out, and_4_out, and_5_out, and_6_out, n1_bit_1_carry_2, n1_bit_2_carry_2,
       n1_bit_3_carry_2, n4_bit_1_out_5, n4_bit_2_out_5, nor_1_out, or_1_out, or_3_out, or_5_out;
  wire [3:0] controlled_buffer_1_out, multiplexer_1_out, multiplexer_2_out, n1_bit_1_result, n4_bit_1_out_4,
       n4_bit_2_out_4, n4_bit_3_out_4, n4_bit_4_out_4;

  _4_bit u_4_bit_1 (.in_1(in_3), .in_3(in_4), .out_5(n4_bit_1_out_5), .out_4(n4_bit_1_out_4));  // open: in_2
  Pull_Resistor pull_resistor_1 (.node(in_2));
  or or_1 (or_1_out, n4_bit_1_out_4[0], n4_bit_1_out_4[1], n4_bit_1_out_4[2], n4_bit_1_out_4[3], ~in_6);  // OR_Gate
  and and_1 (and_1_out, or_1_out, ~n4_bit_1_out_5, in_2);  // AND_Gate
  _4_bit u_4_bit_2 (.in_1(in_3), .in_3(in_4), .in_2(and_1_out), .out_5(n4_bit_2_out_5), .out_4(n4_bit_2_out_4));
  or or_2 (out_12, n4_bit_2_out_5, and_2_out);
  Multiplexer #(.width(4), .enable("false")) multiplexer_1 (
    .in0(n4_bit_2_out_4), .in1(n4_bit_3_out_4), .out(multiplexer_1_out), .sel(n4_bit_2_out_5));
  _4_bit u_4_bit_3 (.in_1(n4_bit_2_out_4), .in_3(4'b0110), .out_4(n4_bit_3_out_4));  // open: in_2, out_5
  assign controlled_buffer_1_out = or_3_out ? 4'b1010 : 4'bz;  // Controlled_Buffer controlled_buffer_1
  Pull_Resistor pull_resistor_2 (.node(controlled_buffer_1_out));
  nor nor_1 (nor_1_out, ~in_6, n4_bit_1_out_4[0], n4_bit_1_out_4[1], n4_bit_1_out_4[2], n4_bit_1_out_4[3]);  // NOR_Gate
  or or_3 (or_3_out, multiplexer_1_out[3], multiplexer_1_out[2], multiplexer_1_out[1], multiplexer_1_out[0]);
  _1_bit u_1_bit_1 (
    .First_number(controlled_buffer_1_out[0]), .Second_number(multiplexer_1_out[0]),
    .Carry_2(n1_bit_1_carry_2), .Result(n1_bit_1_result[0]));  // open: Carry
  _1_bit u_1_bit_2 (
    .First_number(controlled_buffer_1_out[1]), .Second_number(multiplexer_1_out[1]),
    .Carry(n1_bit_1_carry_2), .Carry_2(n1_bit_2_carry_2), .Result(n1_bit_1_result[1]));
  _1_bit u_1_bit_3 (
    .First_number(controlled_buffer_1_out[2]), .Second_number(multiplexer_1_out[2]),
    .Carry(n1_bit_2_carry_2), .Carry_2(n1_bit_3_carry_2), .Result(n1_bit_1_result[2]));
  _1_bit u_1_bit_4 (
    .First_number(controlled_buffer_1_out[3]), .Second_number(multiplexer_1_out[3]),
    .Carry(n1_bit_3_carry_2), .Result(n1_bit_1_result[3]));  // open: Carry_2
  and and_2 (and_2_out, nor_1_out, in_2, in_6);
  Multiplexer #(.width(4), .enable("false")) multiplexer_2 (
    .in0(multiplexer_1_out), .in1(n1_bit_1_result), .out(multiplexer_2_out), .sel(and_3_out));
  and and_3 (and_3_out, or_3_out, out_8);
  or or_4 (out_8, in_5, and_2_out, and_4_out);
  and and_4 (and_4_out, n4_bit_2_out_5, in_6);
  Pull_Resistor #(.pull(1)) pull_resistor_3 (.node(in_6));
  Pull_Resistor pull_resistor_4 (.node(in_5));
  Multiplexer #(.width(4), .enable("false")) multiplexer_3 (
    .in0(multiplexer_2_out), .in1(n4_bit_4_out_4), .out(out_11), .sel(and_5_out));
  _4_bit u_4_bit_4 (.in_1(multiplexer_2_out), .in_3(4'b0001), .out_4(n4_bit_4_out_4));  // open: in_2, out_5
  and and_5 (and_5_out, ~and_6_out, n4_bit_2_out_5, or_5_out, ~in_1);  // AND_Gate
  or or_5 (or_5_out, in_6, in_7);
  and and_6 (and_6_out, in_2, in_6);
  Pull_Resistor pull_resistor_5 (.node(in_1));
  nor nor_2 (out_10, out_11[3], out_11[2], out_11[1], out_11[0]);
  Pull_Resistor pull_resistor_6 (.node(in_7));

  assign out_9 = 1'b0;
  assign out_13 = out_10;
endmodule

module _1_bit_2 (
  input  in_1,
  input  in_2,
  input  in_3,
  output out_4,
  output out_5
);

  Pull_Resistor pull_resistor_1 (.node(in_1));
  BitAdder #(.width(1)) bitadder_1 (.in0(in_2), .in1(in_1), .in2(in_3), .out({out_5, out_4}));
endmodule

module _4_bit_2 (
  input  [3:0] in_1,
  input  in_2,
  input  [3:0] in_3,
  output [3:0] out_4,
  output out_5
);

  wire n1_bit_1_out_5, n1_bit_2_out_5, n1_bit_3_out_5;

  Pull_Resistor pull_resistor_1 (.node(in_3));
  Pull_Resistor pull_resistor_2 (.node(in_2));
  _1_bit_2 u_1_bit_1 (.in_2(in_1[0]), .in_3(in_3[0]), .in_1(in_2), .out_5(n1_bit_1_out_5), .out_4(out_4[0]));
  _1_bit_2 u_1_bit_2 (.in_2(in_1[1]), .in_3(in_3[1]), .in_1(n1_bit_1_out_5), .out_5(n1_bit_2_out_5), .out_4(out_4[1]));
  _1_bit_2 u_1_bit_3 (.in_2(in_1[2]), .in_3(in_3[2]), .in_1(n1_bit_2_out_5), .out_5(n1_bit_3_out_5), .out_4(out_4[2]));
  _1_bit_2 u_1_bit_4 (.in_2(in_1[3]), .in_3(in_3[3]), .in_1(n1_bit_3_out_5), .out_5(out_5), .out_4(out_4[3]));
endmodule

module Base_10_plus_module (
  input  in_1,
  input  [3:0] in_2,
  input  [3:0] in_3,
  output [3:0] out_4,
  output out_5
);

  wire and_1_out, n4_bit_1_out_5, or_1_out;
  wire [3:0] n4_bit_1_out_4, n4_bit_2_out_4;

  Pull_Resistor pull_resistor_1 (.node(in_1));
  _4_bit_2 u_4_bit_1 (.in_1(in_2), .in_3(in_3), .in_2(in_1), .out_5(n4_bit_1_out_5), .out_4(n4_bit_1_out_4));
  or or_1 (or_1_out, n4_bit_1_out_4[1], n4_bit_1_out_4[2]);
  and and_1 (and_1_out, or_1_out, n4_bit_1_out_4[3]);
  Multiplexer #(.width(4), .enable("false")) multiplexer_1 (
    .in0(n4_bit_1_out_4), .in1(n4_bit_2_out_4), .out(out_4), .sel(out_5));
  _4_bit u_4_bit_2 (.in_1(n4_bit_1_out_4), .in_3(4'b1010), .out_4(n4_bit_2_out_4));  // open: in_2, out_5
  or or_2 (out_5, and_1_out, n4_bit_1_out_5);
endmodule

module circuit_2 (
  input  in_1,
  output [4:0] out_2,
  output [4:0] out_3,
  output [4:0] out_4,
  output [4:0] out_5,
  output [4:0] out_6
);


  assign out_2 = {5{1'b0}};
  assign out_3 = {1'b0, in_1, 1'b0, in_1, 1'b0};
  assign out_4 = {1'b0, in_1, 1'b0, in_1, 1'b0};
  assign out_5 = {1'b0, in_1, 1'b0, in_1, 1'b0};
  assign out_6 = {5{1'b0}};
endmodule
